// Digital circuit frontpanel.dig as structural Verilog
module frontpanel (
  input  [15:0] A,
  input  [15:0] B,
  input  [15:0] A_2,
  input  [15:0] B_2,
  input  [15:0] A_3,
  input  [15:0] B_3,
  input  [15:0] A_4,
  input  [15:0] B_4,
  output [15:0] O,
  output [15:0] O_2,
  output [15:0] O_3,
  output [15:0] O_4
);

  wire button_1_out, decoder_1_p2, decoder_1_p3, demultiplexer_2_out_0, demultiplexer_2_out_1,
       demultiplexer_2_out_2, demultiplexer_2_out_3;
  wire [1:0] PC_out;
  wire [15:0] demultiplexer_1_out_0, demultiplexer_1_out_1, demultiplexer_1_out_2, demultiplexer_1_out_3,
       execute_1_p3, multiplexer_2_out, multiplexer_3_out, multiplexer_4_out, multiplexer_5_out;
  wire [31:0] multiplexer_1_out;

  Counter #(.Bits(2)) PC (.en(1'b1), .C(button_1_out), .clr(1'b0), .out(PC_out));  // open: ovf
  Button button_1 (.out(button_1_out));
  Multiplexer #(.Bits(32), .Selector_Bits(2)) multiplexer_1 (
    .sel(PC_out), .in_0({B, A}), .in_1({B_2, A_2}), .in_2({B_3, A_3}), .in_3({B_4, A_4}),
    .out(multiplexer_1_out));
  // decoder decoder_1: pin names not known; wires that end beside it: multiplexer_1_out, decoder_1_p2, decoder_1_p3
  // execute execute_1: pin names not known; wires that end beside it: decoder_1_p2, decoder_1_p3, execute_1_p3
  Demultiplexer #(.Bits(16), .Selector_Bits(2)) demultiplexer_1 (
    .sel(PC_out), .in(execute_1_p3), .out_0(demultiplexer_1_out_0), .out_1(demultiplexer_1_out_1),
    .out_2(demultiplexer_1_out_2), .out_3(demultiplexer_1_out_3));
  Demultiplexer #(.Selector_Bits(2)) demultiplexer_2 (
    .sel(PC_out), .in(1'b1), .out_0(demultiplexer_2_out_0), .out_1(demultiplexer_2_out_1),
    .out_2(demultiplexer_2_out_2), .out_3(demultiplexer_2_out_3));
  Multiplexer #(.Bits(16)) multiplexer_2 (
    .sel(demultiplexer_2_out_0), .in_0(O), .in_1(demultiplexer_1_out_0), .out(multiplexer_2_out));
  Multiplexer #(.Bits(16)) multiplexer_3 (
    .sel(demultiplexer_2_out_1), .in_0(O_2), .in_1(demultiplexer_1_out_1), .out(multiplexer_3_out));
  Multiplexer #(.Bits(16)) multiplexer_4 (
    .sel(demultiplexer_2_out_2), .in_0(O_3), .in_1(demultiplexer_1_out_2), .out(multiplexer_4_out));
  Multiplexer #(.Bits(16)) multiplexer_5 (
    .sel(demultiplexer_2_out_3), .in_0(O_4), .in_1(demultiplexer_1_out_3), .out(multiplexer_5_out));
  D_FF #(.Bits(16)) d_ff_1 (.D(multiplexer_2_out), .C(button_1_out), .Q(O));  // open: nQ
  D_FF #(.Bits(16)) d_ff_2 (.D(multiplexer_3_out), .C(button_1_out), .Q(O_2));  // open: nQ
  D_FF #(.Bits(16)) d_ff_3 (.D(multiplexer_4_out), .C(button_1_out), .Q(O_3));  // open: nQ
  D_FF #(.Bits(16)) d_ff_4 (.D(multiplexer_5_out), .C(button_1_out), .Q(O_4));  // open: nQ

  // Notes on the sheet:
  //   A: default 100
  //   B: default 54
  //   A_2: default 200
  //   B_2: default 42
  //   A_3: default 99
  //   B_3: default 1
  //   A_4: default 34
  //   B_4: default 26
endmodule
